// Logisim project CPU.circ as structural Verilog: 10 circuits, main circuit main
module main (
  input  siempre_uno,
  input  in_2,
  input  in_3,
  output out_4,
  output out_5,
  output out_6,
  output out_7,
  output out_8,
  output out_9
);

  wire clock_1_out, controlled_buffer_1_out, demultiplexer_1_out0, demultiplexer_1_out1,
       demultiplexer_1_out2, demultiplexer_1_out3, demultiplexer_1_out4, demultiplexer_1_out5,
       demultiplexer_1_out6, demultiplexer_1_out7, demultiplexer_1_out8, demultiplexer_1_out10,
       demultiplexer_1_out11, n7_segments_hex_1_a, n7_segments_hex_1_b, n7_segments_hex_1_c,
       n7_segments_hex_1_d, n7_segments_hex_1_e, n7_segments_hex_1_f, n7_segments_hex_1_g, nor_1_out,
       not_1_out, not_2_out, or_1_out, or_2_out, or_3_out, or_4_out, registros_1_out_2_1,
       registros_1_out_2_2, registros_1_out_2_3, registros_1_out_2_4;
  wire [3:0] controlled_buffer_2_out, controlled_buffer_5_out, counter_1_q, registros_1_out_1_4;
  wire [15:0] rom_1_data;

  or or_1 (or_1_out, controlled_buffer_1_out, demultiplexer_1_out6);
  assign controlled_buffer_1_out = demultiplexer_1_out7 ? nor_1_out : 1'bz;  // Controlled_Buffer controlled_buffer_1
  Counter #(.width(4), .max('hf)) counter_1 (
    .load(or_1_out), .D(rom_1_data[5:2]), .count(not_1_out), .Q(counter_1_q), .clk(clock_1_out));  // open: carry, clr
  not not_1 (not_1_out, or_1_out);
  nor nor_1 (nor_1_out, registros_1_out_1_4[0], registros_1_out_1_4[1], registros_1_out_1_4[2], registros_1_out_1_4[3]);
  Clock #(.highDuration(2), .lowDuration(2)) clock_1 (.out(clock_1_out));
  ROM #(.addrWidth(4), .dataWidth(16)) rom_1 (.addr(counter_1_q), .data(rom_1_data), .sel(siempre_uno));
  not not_2 (not_2_out, clock_1_out);
  Demultiplexer #(.select(4)) demultiplexer_1 (
    .out0(demultiplexer_1_out0), .out1(demultiplexer_1_out1), .out2(demultiplexer_1_out2),
    .out3(demultiplexer_1_out3), .out4(demultiplexer_1_out4), .out5(demultiplexer_1_out5),
    .out6(demultiplexer_1_out6), .out7(demultiplexer_1_out7), .out8(demultiplexer_1_out8),
    .out10(demultiplexer_1_out10), .out11(demultiplexer_1_out11), .in(in_2), .sel(rom_1_data[15:12]),
    .en(in_2));  // open: out9, out12, out13, out14, out15
  or or_2 (or_2_out, demultiplexer_1_out0, demultiplexer_1_out1, demultiplexer_1_out2, demultiplexer_1_out3, demultiplexer_1_out4, demultiplexer_1_out5);
  or or_3 (or_3_out, demultiplexer_1_out8, demultiplexer_1_out10);
  or or_4 (or_4_out, or_2_out, or_3_out);
  assign controlled_buffer_2_out = demultiplexer_1_out10 ? rom_1_data[5:2] : 4'bz;  // Controlled_Buffer controlled_buffer_2
  assign controlled_buffer_2_out = demultiplexer_1_out8 ? registros_1_out_1_4 : 4'bz;  // Controlled_Buffer controlled_buffer_3
  assign controlled_buffer_2_out = or_2_out ? {out_4, out_5, out_6, out_7} : 4'bz;  // Controlled_Buffer controlled_buffer_4
  REGISTROS registros_1 (
    .write_enable(or_4_out), .always_on(in_3), .clock(not_2_out), .in_1(controlled_buffer_2_out[3]),
    .in_2(controlled_buffer_2_out[2]), .in_3(controlled_buffer_2_out[1]), .in_4(controlled_buffer_2_out[0]),
    .address_1_1(rom_1_data[11]), .address_2_1(rom_1_data[9]), .address_1_2(rom_1_data[10]),
    .address_2_2(rom_1_data[8]), .address_in_1(rom_1_data[7]), .address_in_2(rom_1_data[6]),
    .out_1_1(registros_1_out_1_4[3]), .out_1_2(registros_1_out_1_4[2]), .out_1_3(registros_1_out_1_4[1]),
    .out_1_4(registros_1_out_1_4[0]), .out_2_1(registros_1_out_2_1), .out_2_2(registros_1_out_2_2),
    .out_2_3(registros_1_out_2_3), .out_2_4(registros_1_out_2_4));
  _7_segments_hex u_7_segments_hex_1 (
    .x1(controlled_buffer_5_out[3]), .x2(controlled_buffer_5_out[2]), .x3(controlled_buffer_5_out[1]),
    .x4(controlled_buffer_5_out[0]), .a(n7_segments_hex_1_a), .b(n7_segments_hex_1_b),
    .c(n7_segments_hex_1_c), .d(n7_segments_hex_1_d), .e(n7_segments_hex_1_e), .f(n7_segments_hex_1_f),
    .g(n7_segments_hex_1_g));
  assign controlled_buffer_5_out = demultiplexer_1_out11 ? registros_1_out_1_4 : 4'bz;  // Controlled_Buffer controlled_buffer_5
  LED led_1 (.in(registros_1_out_1_4[3]));
  LED led_2 (.in(registros_1_out_1_4[2]));
  _7_Segment_Display u_7_segment_display_1 (
    .g(n7_segments_hex_1_g), .f(n7_segments_hex_1_f), .a(n7_segments_hex_1_a), .b(n7_segments_hex_1_b),
    .e(n7_segments_hex_1_e), .d(n7_segments_hex_1_d), .c(n7_segments_hex_1_c));  // open: dp
  LED led_3 (.in(registros_1_out_1_4[1]));
  LED led_4 (.in(registros_1_out_1_4[0]));
  LED led_5 (.in(registros_1_out_2_1));
  LED led_6 (.in(registros_1_out_2_2));
  LED led_7 (.in(registros_1_out_2_3));
  LED led_8 (.in(registros_1_out_2_4));
  ALU alu_1 (
    .enable_del_dmx(or_2_out), .in1(registros_1_out_1_4[3]), .in2(registros_1_out_1_4[2]),
    .in3(registros_1_out_1_4[1]), .in4(registros_1_out_1_4[0]), .in5(registros_1_out_2_1),
    .in6(registros_1_out_2_2), .in7(registros_1_out_2_3), .in8(registros_1_out_2_4),
    .opcode_1(rom_1_data[15]), .opcode_2(rom_1_data[14]), .opcode3(rom_1_data[13]),
    .opcode_4(rom_1_data[12]), .clock(in_3), .Overflow(out_8), .Overflow_2(out_9), .out_1(out_4),
    .out_2(out_5), .out_3(out_6), .out_4(out_7));

  // Notes on the sheet:
  //   contents of rom_1 (hex, n*v repeats v):
  //   0 a014 a048 a084 7020 47c0 5200 6010 bc00
endmodule

module ALU (
  input  clock,
  input  enable_del_dmx,
  input  opcode_1,
  input  opcode_2,
  input  opcode3,
  input  opcode_4,
  input  in1,
  input  in2,
  input  in3,
  input  in4,
  input  in5,
  input  in6,
  input  in7,
  input  in8,
  output out_1,
  output out_2,
  output out_3,
  output out_4,
  output Overflow,
  output Overflow_2
);

  wire add_1_out_10, add_1_out_11, add_1_out_12, add_1_out_13, and_1_out, and_2_out, and_3_out, and_4_out,
       demultiplexer_1_out0, demultiplexer_1_out1, demultiplexer_1_out2, demultiplexer_1_out3,
       demultiplexer_1_out4, demultiplexer_1_out5, not_1_out, or_1_out, or_2_out, or_3_out, or_4_out,
       subs_1_out_10, subs_1_out_11, subs_1_out_12, subs_1_out_13, xor_1_out, xor_2_out, xor_3_out, xor_4_out;

  assign out_1 = demultiplexer_1_out0 ? and_1_out : 1'bz;  // Controlled_Buffer controlled_buffer_1
  and and_1 (and_1_out, in1, in5);
  assign out_2 = demultiplexer_1_out0 ? and_2_out : 1'bz;  // Controlled_Buffer controlled_buffer_2
  and and_2 (and_2_out, in2, in6);
  assign out_3 = demultiplexer_1_out0 ? and_3_out : 1'bz;  // Controlled_Buffer controlled_buffer_3
  and and_3 (and_3_out, in3, in7);
  assign out_4 = demultiplexer_1_out0 ? and_4_out : 1'bz;  // Controlled_Buffer controlled_buffer_4
  and and_4 (and_4_out, in4, in8);
  or or_1 (or_1_out, in1, in5);
  assign out_1 = demultiplexer_1_out1 ? or_1_out : 1'bz;  // Controlled_Buffer controlled_buffer_5
  assign out_2 = demultiplexer_1_out1 ? or_2_out : 1'bz;  // Controlled_Buffer controlled_buffer_6
  or or_2 (or_2_out, in2, in6);
  or or_3 (or_3_out, in3, in7);
  assign out_3 = demultiplexer_1_out1 ? or_3_out : 1'bz;  // Controlled_Buffer controlled_buffer_7
  or or_4 (or_4_out, in4, in8);
  assign out_4 = demultiplexer_1_out1 ? or_4_out : 1'bz;  // Controlled_Buffer controlled_buffer_8
  assign out_1 = demultiplexer_1_out2 ? xor_1_out : 1'bz;  // Controlled_Buffer controlled_buffer_9
  xor xor_1 (xor_1_out, in1, in5);
  xor xor_2 (xor_2_out, in2, in6);
  assign out_2 = demultiplexer_1_out2 ? xor_2_out : 1'bz;  // Controlled_Buffer controlled_buffer_10
  assign out_3 = demultiplexer_1_out2 ? xor_3_out : 1'bz;  // Controlled_Buffer controlled_buffer_11
  xor xor_3 (xor_3_out, in3, in7);
  xor xor_4 (xor_4_out, in4, in8);
  assign out_1 = demultiplexer_1_out3 ? ~in1 : 1'bz;  // Controlled_Inverter controlled_inverter_1
  assign out_2 = demultiplexer_1_out3 ? ~in2 : 1'bz;  // Controlled_Inverter controlled_inverter_2
  assign out_3 = demultiplexer_1_out3 ? ~in3 : 1'bz;  // Controlled_Inverter controlled_inverter_3
  not not_1 (not_1_out, demultiplexer_1_out4);
  assign out_4 = demultiplexer_1_out4 ? add_1_out_10 : 1'bz;  // Controlled_Buffer controlled_buffer_12
  ADD add_1 (
    .A0(in4), .A1(in3), .A2(in2), .A3(in1), .B0(in8), .B1(in7), .B2(in6), .B3(in5), .in_1(not_1_out),
    .Overflow(Overflow), .out_10(add_1_out_10), .out_11(add_1_out_11), .out_12(add_1_out_12),
    .out_13(add_1_out_13));
  assign out_3 = demultiplexer_1_out4 ? add_1_out_11 : 1'bz;  // Controlled_Buffer controlled_buffer_13
  assign out_2 = demultiplexer_1_out4 ? add_1_out_12 : 1'bz;  // Controlled_Buffer controlled_buffer_14
  assign out_4 = demultiplexer_1_out5 ? subs_1_out_10 : 1'bz;  // Controlled_Buffer controlled_buffer_15
  SUBS subs_1 (
    .A0(in4), .A1(in3), .A2(in2), .A3(in1), .B0(in8), .B1(in7), .B2(in6), .B3(in5),
    .in_2(demultiplexer_1_out5), .Overflow(Overflow_2), .out_10(subs_1_out_10), .out_11(subs_1_out_11),
    .out_12(subs_1_out_12), .out_13(subs_1_out_13));
  assign out_3 = demultiplexer_1_out5 ? subs_1_out_11 : 1'bz;  // Controlled_Buffer controlled_buffer_16
  assign out_2 = demultiplexer_1_out5 ? subs_1_out_12 : 1'bz;  // Controlled_Buffer controlled_buffer_17
  Demultiplexer #(.select(4)) demultiplexer_1 (
    .out0(demultiplexer_1_out0), .out1(demultiplexer_1_out1), .out2(demultiplexer_1_out2),
    .out3(demultiplexer_1_out3), .out4(demultiplexer_1_out4), .out5(demultiplexer_1_out5), .in(clock),
    .sel({opcode_1, opcode_2, opcode3, opcode_4}), .en(enable_del_dmx));  // open: out6, out7, out8, out9, out10, out11, out12, out13, out14, out15
  assign out_4 = demultiplexer_1_out2 ? xor_4_out : 1'bz;  // Controlled_Buffer controlled_buffer_18
  assign out_4 = demultiplexer_1_out3 ? ~in4 : 1'bz;  // Controlled_Inverter controlled_inverter_4
  assign out_1 = demultiplexer_1_out4 ? add_1_out_13 : 1'bz;  // Controlled_Buffer controlled_buffer_19
  assign out_1 = demultiplexer_1_out5 ? subs_1_out_13 : 1'bz;  // Controlled_Buffer controlled_buffer_20
endmodule

module ADD (
  input  in_1,
  input  A0,
  input  A1,
  input  A2,
  input  A3,
  input  B0,
  input  B1,
  input  B2,
  input  B3,
  output out_10,
  output out_11,
  output out_12,
  output out_13,
  output Overflow
);

  wire n1_bit_adder_1_c_out, n1_bit_adder_2_c_out, n1_bit_adder_3_c_out;

  _1_bit_adder u_1_bit_adder_1 (.A(A0), .B(B0), .C_in(in_1), .C_out(n1_bit_adder_1_c_out), .Sum(out_10));
  _1_bit_adder u_1_bit_adder_2 (
    .A(A1), .B(B1), .C_in(n1_bit_adder_1_c_out), .C_out(n1_bit_adder_2_c_out), .Sum(out_11));
  _1_bit_adder u_1_bit_adder_3 (
    .A(A2), .B(B2), .C_in(n1_bit_adder_2_c_out), .C_out(n1_bit_adder_3_c_out), .Sum(out_12));
  _1_bit_adder u_1_bit_adder_4 (.A(A3), .B(B3), .C_in(n1_bit_adder_3_c_out), .C_out(Overflow), .Sum(out_13));
endmodule

module _1_bit_adder (
  input  C_in,
  input  A,
  input  B,
  output Sum,
  output C_out
);

  wire and_1_out, and_2_out, and_3_out, xor_2_out;

  and and_1 (and_1_out, C_in, A);
  and and_2 (and_2_out, C_in, B);
  and and_3 (and_3_out, A, B);
  xor xor_1 (Sum, C_in, xor_2_out);
  xor xor_2 (xor_2_out, A, B);
  or or_1 (C_out, and_1_out, and_2_out, and_3_out);
endmodule

module SUBS (
  input  A0,
  input  in_2,
  input  A1,
  input  A2,
  input  A3,
  input  B0,
  input  B1,
  input  B2,
  input  B3,
  output out_10,
  output out_11,
  output out_12,
  output out_13,
  output Overflow
);

  wire n1_bit_adder_1_c_out, n1_bit_adder_2_c_out, n1_bit_adder_3_c_out, not_1_out, not_2_out, not_3_out,
       not_4_out;

  not not_1 (not_1_out, B2);
  not not_2 (not_2_out, B0);
  not not_3 (not_3_out, B1);
  not not_4 (not_4_out, B3);
  _1_bit_adder u_1_bit_adder_1 (.A(A0), .B(not_2_out), .C_in(in_2), .C_out(n1_bit_adder_1_c_out), .Sum(out_10));
  _1_bit_adder u_1_bit_adder_2 (
    .A(A1), .B(not_3_out), .C_in(n1_bit_adder_1_c_out), .C_out(n1_bit_adder_2_c_out), .Sum(out_11));
  _1_bit_adder u_1_bit_adder_3 (
    .A(A2), .B(not_1_out), .C_in(n1_bit_adder_2_c_out), .C_out(n1_bit_adder_3_c_out), .Sum(out_12));
  _1_bit_adder u_1_bit_adder_4 (.A(A3), .B(not_4_out), .C_in(n1_bit_adder_3_c_out), .C_out(Overflow), .Sum(out_13));
endmodule

module REGISTROS (
  input  write_enable,
  input  address_1_1,
  input  address_1_2,
  input  address_2_1,
  input  address_2_2,
  input  address_in_1,
  input  address_in_2,
  input  always_on,
  input  clock,
  input  in_1,
  input  in_2,
  input  in_3,
  input  in_4,
  output out_1_1,
  output out_1_2,
  output out_1_3,
  output out_1_4,
  output out_2_1,
  output out_2_2,
  output out_2_3,
  output out_2_4
);

  wire demultiplexer_1_out0, demultiplexer_1_out1, demultiplexer_1_out2, demultiplexer_1_out3, register_1_q,
       register_2_q, register_3_q, register_4_q, register_5_q, register_6_q, register_7_q, register_8_q,
       register_9_q, register_10_q, register_11_q, register_12_q, register_13_q, register_14_q,
       register_15_q, register_16_q;

  Demultiplexer #(.select(2)) demultiplexer_1 (
    .out0(demultiplexer_1_out0), .out1(demultiplexer_1_out1), .out2(demultiplexer_1_out2),
    .out3(demultiplexer_1_out3), .in(clock), .sel({address_in_1, address_in_2}), .en(write_enable));
  Register #(.width(1)) register_1 (.D(in_1), .Q(register_1_q), .clk(demultiplexer_1_out0));  // open: en, clr
  Register #(.width(1)) register_2 (.D(in_2), .Q(register_2_q), .clk(demultiplexer_1_out0));  // open: en, clr
  Register #(.width(1)) register_3 (.D(in_3), .Q(register_3_q), .clk(demultiplexer_1_out0));  // open: en, clr
  Register #(.width(1)) register_4 (.D(in_4), .Q(register_4_q), .clk(demultiplexer_1_out0));  // open: en, clr
  Register #(.width(1)) register_5 (.D(in_1), .Q(register_5_q), .clk(demultiplexer_1_out1));  // open: en, clr
  Register #(.width(1)) register_6 (.D(in_2), .Q(register_6_q), .clk(demultiplexer_1_out1));  // open: en, clr
  Register #(.width(1)) register_7 (.D(in_3), .Q(register_7_q), .clk(demultiplexer_1_out1));  // open: en, clr
  Register #(.width(1)) register_8 (.D(in_4), .Q(register_8_q), .clk(demultiplexer_1_out1));  // open: en, clr
  Register #(.width(1)) register_9 (.D(in_1), .Q(register_9_q), .clk(demultiplexer_1_out2));  // open: en, clr
  Register #(.width(1)) register_10 (.D(in_2), .Q(register_10_q), .clk(demultiplexer_1_out2));  // open: en, clr
  Register #(.width(1)) register_11 (.D(in_3), .Q(register_11_q), .clk(demultiplexer_1_out2));  // open: en, clr
  Register #(.width(1)) register_12 (.D(in_4), .Q(register_12_q), .clk(demultiplexer_1_out2));  // open: en, clr
  Register #(.width(1)) register_13 (.D(in_1), .Q(register_13_q), .clk(demultiplexer_1_out3));  // open: en, clr
  Register #(.width(1)) register_14 (.D(in_2), .Q(register_14_q), .clk(demultiplexer_1_out3));  // open: en, clr
  Register #(.width(1)) register_15 (.D(in_3), .Q(register_15_q), .clk(demultiplexer_1_out3));  // open: en, clr
  Register #(.width(1)) register_16 (.D(in_4), .Q(register_16_q), .clk(demultiplexer_1_out3));  // open: en, clr
  Multiplexer #(.select(2)) multiplexer_1 (
    .in0(register_1_q), .in1(register_5_q), .in2(register_9_q), .in3(register_13_q), .out(out_1_1),
    .sel({address_1_1, address_1_2}), .en(always_on));
  Multiplexer #(.select(2)) multiplexer_2 (
    .in0(register_2_q), .in1(register_6_q), .in2(register_10_q), .in3(register_14_q), .out(out_1_2),
    .sel({address_1_1, address_1_2}), .en(always_on));
  Multiplexer #(.select(2)) multiplexer_3 (
    .in0(register_3_q), .in1(register_7_q), .in2(register_11_q), .in3(register_15_q), .out(out_1_3),
    .sel({address_1_1, address_1_2}), .en(always_on));
  Multiplexer #(.select(2)) multiplexer_4 (
    .in0(register_4_q), .in1(register_8_q), .in2(register_12_q), .in3(register_16_q), .out(out_1_4),
    .sel({address_1_1, address_1_2}), .en(always_on));
  Multiplexer #(.select(2)) multiplexer_5 (
    .in0(register_1_q), .in1(register_5_q), .in2(register_9_q), .in3(register_13_q), .out(out_2_1),
    .sel({address_2_1, address_2_2}), .en(always_on));
  Multiplexer #(.select(2)) multiplexer_6 (
    .in0(register_2_q), .in1(register_6_q), .in2(register_10_q), .in3(register_14_q), .out(out_2_2),
    .sel({address_2_1, address_2_2}), .en(always_on));
  Multiplexer #(.select(2)) multiplexer_7 (
    .in0(register_3_q), .in1(register_7_q), .in2(register_11_q), .in3(register_15_q), .out(out_2_3),
    .sel({address_2_1, address_2_2}), .en(always_on));
  Multiplexer #(.select(2)) multiplexer_8 (
    .in0(register_4_q), .in1(register_8_q), .in2(register_12_q), .in3(register_16_q), .out(out_2_4),
    .sel({address_2_1, address_2_2}), .en(always_on));
endmodule

module _7_segments_hex (
  input  x1,
  input  x2,
  input  x3,
  input  x4,
  output a,
  output b,
  output c,
  output d,
  output e,
  output f,
  output g
);

  wire and_1_out, and_2_out, and_3_out, and_4_out, and_5_out, and_6_out, and_7_out, and_8_out, and_9_out,
       and_10_out, and_11_out, and_12_out, and_13_out, and_14_out, and_15_out, and_16_out, and_17_out,
       and_18_out, and_19_out, and_20_out, and_21_out, and_22_out, and_23_out, and_24_out, and_25_out,
       and_26_out, and_27_out, and_28_out, and_29_out, and_30_out, and_31_out, and_32_out, and_33_out,
       not_1_out, not_2_out, not_3_out, not_4_out, not_5_out, not_6_out, not_7_out, not_8_out, not_9_out,
       not_10_out, not_11_out, not_12_out, not_13_out, not_14_out, not_15_out, not_16_out, not_17_out,
       not_18_out, not_19_out, not_20_out, not_21_out, not_22_out, not_23_out, not_24_out, not_25_out,
       not_26_out, not_27_out, not_28_out, not_29_out, not_30_out, not_31_out, not_32_out, not_33_out,
       not_34_out, not_35_out, not_36_out, not_37_out, not_38_out, not_39_out, not_40_out, not_41_out;

  not not_1 (not_1_out, x2);
  and and_1 (and_1_out, not_1_out, not_2_out);
  not not_2 (not_2_out, x4);
  not not_3 (not_3_out, x1);
  and and_2 (and_2_out, not_3_out, x3);
  not not_4 (not_4_out, x1);
  and and_3 (and_3_out, not_4_out, x2, x4);
  and and_4 (and_4_out, x2, x3);
  and and_5 (and_5_out, x1, not_5_out, not_6_out);
  not not_5 (not_5_out, x2);
  not not_6 (not_6_out, x3);
  and and_6 (and_6_out, x1, not_7_out);
  not not_7 (not_7_out, x4);
  not not_8 (not_8_out, x1);
  and and_7 (and_7_out, not_8_out, not_9_out);
  not not_9 (not_9_out, x2);
  not not_10 (not_10_out, x1);
  and and_8 (and_8_out, not_10_out, not_11_out, not_12_out);
  not not_11 (not_11_out, x3);
  not not_12 (not_12_out, x4);
  not not_13 (not_13_out, x2);
  and and_9 (and_9_out, not_13_out, not_14_out);
  not not_14 (not_14_out, x4);
  not not_15 (not_15_out, x1);
  and and_10 (and_10_out, not_15_out, x3, x4);
  not not_16 (not_16_out, x3);
  and and_11 (and_11_out, x1, not_16_out, x4);
  not not_17 (not_17_out, x1);
  and and_12 (and_12_out, not_17_out, not_18_out);
  not not_18 (not_18_out, x3);
  not not_19 (not_19_out, x1);
  and and_13 (and_13_out, not_19_out, x4);
  not not_20 (not_20_out, x3);
  and and_14 (and_14_out, not_20_out, x4);
  not not_21 (not_21_out, x1);
  and and_15 (and_15_out, not_21_out, x2);
  and and_16 (and_16_out, x1, not_22_out);
  not not_22 (not_22_out, x2);
  not not_23 (not_23_out, x2);
  and and_17 (and_17_out, not_23_out, not_24_out);
  not not_24 (not_24_out, x4);
  not not_25 (not_25_out, x2);
  and and_18 (and_18_out, not_25_out, x3);
  and and_19 (and_19_out, x3, not_26_out);
  not not_26 (not_26_out, x4);
  not not_27 (not_27_out, x3);
  and and_20 (and_20_out, x2, not_27_out, x4);
  and and_21 (and_21_out, x1, not_28_out);
  not not_28 (not_28_out, x3);
  not not_29 (not_29_out, x2);
  and and_22 (and_22_out, not_29_out, not_30_out);
  not not_30 (not_30_out, x4);
  and and_23 (and_23_out, x3, not_31_out);
  not not_31 (not_31_out, x4);
  and and_24 (and_24_out, x1, x3);
  and and_25 (and_25_out, x1, x2);
  not not_32 (not_32_out, x2);
  and and_26 (and_26_out, not_32_out, not_33_out, not_34_out);
  not not_33 (not_33_out, x3);
  not not_34 (not_34_out, x4);
  not not_35 (not_35_out, x1);
  and and_27 (and_27_out, not_35_out, x2, not_36_out);
  not not_36 (not_36_out, x3);
  and and_28 (and_28_out, x2, x3, not_37_out);
  not not_37 (not_37_out, x4);
  not not_38 (not_38_out, x2);
  and and_29 (and_29_out, x1, not_38_out, x4);
  and and_30 (and_30_out, x1, x2, x3);
  not not_39 (not_39_out, x2);
  and and_31 (and_31_out, not_39_out, x3);
  and and_32 (and_32_out, x2, not_40_out);
  not not_40 (not_40_out, x3);
  and and_33 (and_33_out, x2, not_41_out);
  not not_41 (not_41_out, x4);
  or or_1 (b, and_7_out, and_8_out, and_9_out, and_10_out, and_11_out);
  or or_2 (c, and_12_out, and_13_out, and_14_out, and_15_out, and_16_out);
  or or_3 (d, and_17_out, and_18_out, and_19_out, and_20_out, and_21_out);
  or or_4 (e, and_22_out, and_23_out, and_24_out, and_25_out);
  or or_5 (f, and_26_out, and_27_out, and_28_out, and_29_out, and_30_out);
  or or_6 (g, and_31_out, and_32_out, and_33_out, x1);
  or or_7 (a, and_1_out, and_2_out, and_3_out, and_4_out, and_5_out, and_6_out);
endmodule

module output_display (
  input  in_1,
  input  in_2,
  input  in_3,
  input  in_4
);

  wire n7_segments_hex_1_a, n7_segments_hex_1_b, n7_segments_hex_1_c, n7_segments_hex_1_d,
       n7_segments_hex_1_e, n7_segments_hex_1_f, n7_segments_hex_1_g;

  _7_segments_hex u_7_segments_hex_1 (
    .x1(in_1), .x2(in_2), .x3(in_3), .x4(in_4), .a(n7_segments_hex_1_a), .b(n7_segments_hex_1_b),
    .c(n7_segments_hex_1_c), .d(n7_segments_hex_1_d), .e(n7_segments_hex_1_e), .f(n7_segments_hex_1_f),
    .g(n7_segments_hex_1_g));
  _7_Segment_Display u_7_segment_display_1 (
    .g(n7_segments_hex_1_g), .f(n7_segments_hex_1_f), .a(n7_segments_hex_1_a), .b(n7_segments_hex_1_b),
    .e(n7_segments_hex_1_e), .d(n7_segments_hex_1_d), .c(n7_segments_hex_1_c));  // open: dp
endmodule

module counter (
  input  in_1,
  input  [3:0] in_2,
  input  in_3
);

  wire clock_1_out;

  Counter #(.width(4), .max('hf), .ongoal("continue")) counter_1 (
    .load(in_1), .D(in_2), .count(in_3), .clk(clock_1_out));  // open: Q, carry, clr
  Clock clock_1 (.out(clock_1_out));
endmodule

module display (
  input  [6:0] in_1,
  input  in_2
);

  wire clock_1_out, not_1_out, or_1_out;

  or or_1 (or_1_out, clock_1_out, not_1_out);
  Clock clock_1 (.out(clock_1_out));
  not not_1 (not_1_out, clock_1_out);
  TTY tty_1 (.data(in_1), .clk(or_1_out), .we(in_2));  // open: clr
endmodule
